// Digital circuit hw1_adder.dig as structural Verilog
module hw1_adder (
  input  A,
  input  B,
  input  C,
  output sum,
  output carry_out
);

  wire and_1_out, and_2_out, and_3_out, and_4_out, and_5_out, and_6_out, and_7_out, not_1_out, not_2_out,
       not_3_out;

  not not_1 (not_1_out, A);
  not not_2 (not_2_out, B);
  not not_3 (not_3_out, C);
  and and_1 (and_1_out, B, C);
  and and_2 (and_2_out, not_1_out, not_2_out, C);
  and and_3 (and_3_out, A, C, not_2_out);
  and and_4 (and_4_out, not_1_out, B, not_3_out);
  and and_5 (and_5_out, A, B, not_3_out);
  and and_6 (and_6_out, A, not_2_out, not_3_out);
  and and_7 (and_7_out, A, B, C);
  or or_1 (carry_out, and_1_out, and_3_out, and_5_out);
  or or_2 (sum, and_2_out, and_4_out, and_6_out, and_7_out);
endmodule
