// Digital circuit hw1_multiplier.dig as structural Verilog
module hw1_multiplier (
  input  [1:0] A,
  input  [1:0] B,
  output [3:0] P
);

  wire and_1_out, and_3_out, and_4_out, and_5_out;

  and and_1 (and_1_out, A[1], B[1]);
  and and_2 (P[0], A[0], B[0]);
  and and_3 (and_3_out, A[0], B[1]);
  and and_4 (and_4_out, A[1], B[0]);
  xor xor_1 (P[1], and_3_out, and_4_out);
  and and_5 (and_5_out, and_3_out, and_4_out);
  xor xor_2 (P[2], and_5_out, and_1_out);
  and and_6 (P[3], and_1_out, and_5_out);
endmodule
