// Digital circuit hw1_ripplecarry_adder.dig as structural Verilog
module hw1_ripplecarry_adder (
  input  [3:0] A,
  input  [3:0] B,
  output [3:0] Sum,
  output carry_out
);

  wire cis310_fall25_digital_1_p3, cis310_fall25_digital_2_p3, cis310_fall25_digital_3_p3;

  // CIS310_Fall25_Digital cis310_fall25_digital_1: pin names not known; wires that end beside it: A[3], B[3], cis310_fall25_digital_1_p3, Sum[3], carry_out
  // CIS310_Fall25_Digital cis310_fall25_digital_2: pin names not known; wires that end beside it: A[2], B[2], cis310_fall25_digital_2_p3, Sum[2], cis310_fall25_digital_1_p3
  // CIS310_Fall25_Digital cis310_fall25_digital_3: pin names not known; wires that end beside it: A[1], B[1], cis310_fall25_digital_3_p3, Sum[1], cis310_fall25_digital_2_p3
  // CIS310_Fall25_Digital cis310_fall25_digital_4: pin names not known; wires that end beside it: A[0], B[0], 1'b0, Sum[0], cis310_fall25_digital_3_p3
endmodule
